// Logisim project Lab1.circ as structural Verilog
module Add1bit (
  input  A,
  input  B,
  input  C,
  output D,
  output C_out
);

  wire and_1_out, and_2_out, and_3_out, xor_1_out;

  xor xor_1 (xor_1_out, A, B);
  and and_1 (and_1_out, A, B);
  and and_2 (and_2_out, A, C);
  and and_3 (and_3_out, B, C);
  xor xor_2 (D, xor_1_out, C);
  or or_1 (C_out, and_1_out, and_3_out);
endmodule

module Add4bit (
  input  in_1
);

  wire [1:1] undriven;

  Add1bit add1bit_1 ();  // open: A, B, C, D, C_out
  Add1bit add1bit_2 (.A(undriven[1]));  // open: B, C, D, C_out
  Add1bit add1bit_3 ();  // open: A, B, C, D, C_out
  Add1bit add1bit_4 ();  // open: A, B, C, D, C_out
  // Pins of 1 and 2 bits meet at {undriven[1], in_1}
endmodule
